# Fritzing sketch VISTA_DISEÑO (saved by Fritzing 0.9.3b)
breadboards: 1

parts:
  WeMos_D1_Mini1 = WeMos D1 Mini
  U1 = NodeMCU V1.0
  LED4 = smd LED [color="Yellow (595nm)" package="1206 [SMD]"]
  LED6 = smd LED [color="Red (633nm)" package="1206 [SMD]"]
  LED8 = smd LED [color="Red (633nm)" package="1206 [SMD]"]
  LED9 = smd LED [color="Green (570nm)" package="1206 [SMD]"]
  LED10 = smd LED [color="Green (570nm)" package="1206 [SMD]"]
  LED11 = smd LED [color="Green (570nm)" package="1206 [SMD]"]
  LED12 = smd LED [color="Red (633nm)" package="1206 [SMD]"]
  LED13 = smd LED [color="Yellow (595nm)" package="1206 [SMD]"]
  LED14 = smd LED [color="Green (570nm)" package="1206 [SMD]"]
  LED15 = smd LED [color="Red (633nm)" package="1206 [SMD]"]
  LED16 = smd LED [color="White (8000K)" package="1206 [SMD]"]
  LED17 = smd LED [color="White (8000K)" package="1206 [SMD]"]
  LED18 = smd LED [color="White (8000K)" package="1206 [SMD]"]
  LED19 = smd LED [color="White (8000K)" package="1206 [SMD]"]
  VCC1 = 4 x AAA Battery Mount

nets:
  5V: WeMos_D1_Mini1.5V, U1.Vin, VCC1.+
  N1: WeMos_D1_Mini1.D1, LED18.anode
  N2: WeMos_D1_Mini1.D2, LED19.anode
  N3: WeMos_D1_Mini1.D3, LED17.anode
  N4: WeMos_D1_Mini1.D4, LED16.anode
  N5: WeMos_D1_Mini1.G, U1.GND, LED4.cathode, LED6.cathode, LED8.cathode, LED9.cathode, LED10.cathode, LED11.cathode, LED12.cathode, LED13.cathode, LED14.cathode, LED15.cathode, LED16.cathode, LED17.cathode, LED18.cathode, LED19.cathode, VCC1.-
  N6: U1.D1, LED10.anode
  N7: U1.D2, LED4.anode
  N8: U1.D3, LED6.anode
  N9: U1.D4, LED11.anode
  N10: U1.D5, LED12.anode
  N11: U1.D6, LED9.anode
  N12: U1.D8, LED15.anode
  N13: U1.RX, LED13.anode
  N14: U1.TX, LED14.anode

custom parts:
  NodeMCU V1.0: ESP8266 based NodeMCU
