# Fritzing sketch VISTA_ESQUEMATICO (saved by Fritzing 0.9.3b)
breadboards: 2

parts:
  U1 = NodeMCU V1.0
  LED = smd LED [color="Yellow (595nm)" package="1206 [SMD]"]
  LED_2 = smd LED [color="Red (633nm)" package="1206 [SMD]"]
  LED_3 = smd LED [color="Red (633nm)" package="1206 [SMD]"]
  LED_4 = smd LED [color="Green (570nm)" package="1206 [SMD]"]
  LED_5 = smd LED [color="Green (570nm)" package="1206 [SMD]"]
  LED_6 = smd LED [color="Green (570nm)" package="1206 [SMD]"]
  LED_7 = smd LED [color="Red (633nm)" package="1206 [SMD]"]
  LED_8 = smd LED [color="Yellow (595nm)" package="1206 [SMD]"]
  LED_9 = smd LED [color="Green (570nm)" package="1206 [SMD]"]
  LED_10 = smd LED [color="Red (633nm)" package="1206 [SMD]"]
  VCC1 = 4 x AAA Battery Mount
  WeMos_D1_Mini2 = WeMos D1 Mini
  LED_11 = smd LED [color="White (8000K)" package="1206 [SMD]"]
  LED_12 = smd LED [color="White (8000K)" package="1206 [SMD]"]
  LED_13 = smd LED [color="White (8000K)" package="1206 [SMD]"]
  LED_14 = smd LED [color="White (8000K)" package="1206 [SMD]"]
  VCC2 = 4 x AAA Battery Mount

nets:
  N1: U1.D1, LED_2.anode
  N2: U1.D2, LED.anode
  N3: U1.D3, LED_5.anode
  N4: U1.D4, LED_7.anode
  N5: U1.GND, LED.cathode, LED_2.cathode, LED_3.cathode, LED_4.cathode, LED_5.cathode, LED_6.cathode, LED_7.cathode, LED_8.cathode, LED_9.cathode, LED_10.cathode, VCC1.-
  N6: U1.D5, LED_6.anode
  N7: U1.D6, LED_3.anode
  N8: U1.D7, LED_4.anode
  N9: U1.D8, LED_10.anode
  N10: U1.RX, LED_8.anode
  N11: U1.TX, LED_9.anode
  N12: U1.Vin, VCC1.+
  N13: WeMos_D1_Mini2.5V, VCC2.+
  N14: WeMos_D1_Mini2.D1, LED_11.anode
  N15: WeMos_D1_Mini2.D2, LED_12.anode
  N16: WeMos_D1_Mini2.D3, LED_13.anode
  N17: WeMos_D1_Mini2.D4, LED_14.anode
  N18: WeMos_D1_Mini2.G, LED_11.cathode, LED_12.cathode, LED_13.cathode, LED_14.cathode, VCC2.-

custom parts:
  NodeMCU V1.0: ESP8266 based NodeMCU
